// Logisim project FullAdderAndSubtractor.circ as structural Verilog: 2 circuits, main circuit main
module main (
  input  [3:0] A,
  input  Cin,
  input  [3:0] B,
  output [3:0] Sum,
  output Cout
);

  wire fa_1bit_1_cout, fa_1bit_2_cout, fa_1bit_3_cout, xor_1_out, xor_2_out, xor_3_out, xor_4_out;

  xor xor_1 (xor_1_out, Cin, B[0]);
  xor xor_2 (xor_2_out, Cin, B[1]);
  xor xor_3 (xor_3_out, Cin, B[2]);
  xor xor_4 (xor_4_out, Cin, B[3]);
  FA_1bit fa_1bit_1 (.Cin(Cin), .A(A[0]), .B(xor_1_out), .Sum(Sum[0]), .Cout(fa_1bit_1_cout));
  FA_1bit fa_1bit_2 (.Cin(fa_1bit_1_cout), .A(A[1]), .B(xor_2_out), .Sum(Sum[1]), .Cout(fa_1bit_2_cout));
  FA_1bit fa_1bit_3 (.Cin(fa_1bit_2_cout), .A(A[2]), .B(xor_3_out), .Sum(Sum[2]), .Cout(fa_1bit_3_cout));
  FA_1bit fa_1bit_4 (.Cin(fa_1bit_3_cout), .A(A[3]), .B(xor_4_out), .Sum(Sum[3]), .Cout(Cout));
endmodule

module FA_1bit (
  input  Cin,
  input  A,
  input  B,
  output Sum,
  output Cout
);

  wire and_1_out, and_2_out, xor_1_out;

  // Probe on A
  // Probe on B
  xor xor_1 (xor_1_out, A, B);
  and and_1 (and_1_out, B, A);
  // Probe on Cin
  // Probe on xor_1_out
  // Probe on and_1_out
  xor xor_2 (Sum, Cin, xor_1_out);
  and and_2 (and_2_out, Cin, xor_1_out);
  // Probe on Sum
  // Probe on Sum
  // Probe on and_2_out
  or or_1 (Cout, and_2_out, and_1_out);
  // Probe on Cout
endmodule
